# Fritzing sketch led (saved by Fritzing 0.9.3b)
breadboards: 1

parts:
  Raspberry_Pi_1 = Raspberry Pi 3 [part_number=RPI-3-V1.2]
  R1 = Resistor [tolerance=±5% resistance=330 package="0603 [SMD]"]
  LED1 = LED - 3mm [color="Red (633nm)" package="3 mm [THT]"]

nets:
  N1: Raspberry_Pi_1.GPIO4, R1.Pin_1
  N2: Raspberry_Pi_1.GND, LED1.cathode
  N3: R1.Pin_0, LED1.anode
